# Fritzing sketch Dog_Food_Circuit (saved by Fritzing 0.9.3b)
circuit board: 8.46667cm x 5.64444cm
perfboards: 1

parts:
  Part1 = NRF24L01+ Breakout Board
  Part3 = Arduino Pro Mini v13
  Part4 = Adafruit Switched JST Breakout [part_number="Adafruit #1863"]

nets:
  GND: Part1.GND, Part3.GND, Part4.GND
  VCC: Part1.VCC, Part3.VCC
  N1: Part1.CE, Part3.D9_PWM
  N2: Part1.CS, Part3.D10_PWM/SS
  N3: Part1.SCK, Part3.D13/SCK
  N4: Part1.MOSI, Part3.D11_PWM/MOSI
  N5: Part1.MISO, Part3.D12/MISO
  N6: Part3.RAW, Part4.V+

custom parts:
  Adafruit Switched JST Breakout: This switched JST connector is the best way to quickly prototype with our LiPoly batteries. We paired a genuine JST connector with a slide switch that can do up to 600mA. Both are soldered onto a breadboard-friendly breakout. There's two ground pins, one 'switched' power pin, and one pin that is always on. This is compatible with the "JST PH 2-pin" connectors we use in our battery packs..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

// code stored in the sketch: dog_food_rf24.ino
//Send.ino

#include<SPI.h>
#include<RF24.h>
#include <avr/sleep.h>

const int switchPin = 3;
int currentStatus;

// ce, csn pins
RF24 radio(9, 10);

void setup(){
  Serial.begin(9600);
  Serial.println("starting RF24 radio...");
  radio.begin();
  radio.setPALevel(RF24_PA_MAX);
  radio.setChannel(0x76);
  radio.openWritingPipe(0xF0F0F0F0E1LL);
  radio.enableDynamicPayloads();
  radio.powerUp();
  digitalWrite(switchPin, HIGH);
  attachInterrupt(1, wakeUpNow, CHANGE);
}

void sleepNow()         // here we put the arduino to sleep
{
    /* Now is the time to set the sleep mode. In the Atmega8 datasheet
     * http://www.atmel.com/dyn/resources/prod_documents/doc2486.pdf on page 35
     * there is a list of sleep modes which explains which clocks and 
     * wake up sources are available in which sleep mode.
     *
     * In the avr/sleep.h file, the call names of these sleep modes are to be found:
     *
     * The 5 different modes are:
     *     SLEEP_MODE_IDLE         -the least power savings 
     *     SLEEP_MODE_ADC
     *     SLEEP_MODE_PWR_SAVE
     *     SLEEP_MODE_STANDBY
     *     SLEEP_MODE_PWR_DOWN     -the most power savings
     *
     * For now, we want as much power savings as possible, so we 
     * choose the according 
     * sleep mode: SLEEP_MODE_PWR_DOWN
     * 
     */
    Serial.println("sleeping...");  
    set_sleep_mode(SLEEP_MODE_PWR_DOWN);   // sleep mode is set here

    sleep_enable();          // enables the sleep bit in the mcucr register
                             // so sleep is possible. just a safety pin 

    /* Now it is time to enable an interrupt. We do it here so an 
     * accidentally pushed interrupt button doesn't interrupt 
     * our running program. if you want to be able to run 
     * interrupt code besides the sleep function, place it in 
     * setup() for example.
     * 
     * In the function call attachInterrupt(A, B, C)
     * A   can be either 0 or 1 for interrupts on pin 2 or 3.   
     * 
     * B   Name of a function you want to execute at interrupt for A.
     *
     * C   Trigger mode of the interrupt pin. can be:
     *             LOW        a low level triggers
     *             CHANGE     a change in level triggers
     *             RISING     a rising edge of a level triggers
     *             FALLING    a falling edge of a level triggers
     *
     * In all but the IDLE sleep modes only LOW can be used.
     */

    attachInterrupt(1,wakeUpNow, CHANGE); // use interrupt 0 (pin 2) and run function
                                       // wakeUpNow when pin 2 gets LOW 

    sleep_mode();            // here the device is actually put to sleep!!
                             // THE PROGRAM CONTINUES FROM HERE AFTER WAKING UP

    sleep_disable();         // first thing after waking from sleep:
                             // disable sleep...
    detachInterrupt(1);      // disables interrupt 0 on pin 2 so the 
                             // wakeUpNow code will not be executed 
                             // during normal running time.

}

void wakeUpNow() {
  if (digitalRead(switchPin) == LOW) {
    currentStatus = 1;
  } else {
    currentStatus = 0;
  }
}

void loop(){
  delay(100);
  wakeUpNow();
  char charBuf[10];
  String text;
  if (currentStatus > 0) {
    text = "Closed";
    text.toCharArray(charBuf, 10);
    Serial.println("Closed");
  } else {
    text = "Open!!";
    text.toCharArray(charBuf, 10);
    Serial.println("Open");
  }
  radio.write(&charBuf, sizeof(text));
  delay(100);
  sleepNow();  
}
